# Fritzing sketch 2013 Wiring Diagram (saved by Fritzing 0.7.12b)
perfboards: 2

parts:
  U1 = Arduino Mega
  J1 = Basic Servo
  J2 = Basic Servo
  M3 = DC Motor  # not connected
  M4 = DC Motor  # not connected
  MIC1 = Microphone  # not connected
  M5 = DC Motor  # not connected
  J3 = Infrared Proximity Sensor
  J4 = Infrared Proximity Sensor
  J5 = Infrared Proximity Sensor
  J6 = Infrared Proximity Sensor

nets:
  N1: U1.D9, J1.pulse
  N2: U1.D8, J2.pulse
  N3: U1.A0, J4.Vout
  N4: U1.A1, J3.Vout
  N5: U1.A2, J6.Vout
  N6: U1.A3, J5.Vout

notes:
  **Motor Encoder Board**
  4 out
  3 out
  +5 v
  Gnd
  2 out
  1 out
  **Rover 5 Motor Driver Board**
  1G/P/D/C 2G/P/D/C 3G/P/D/C 4G/P/D/C
  G=Ground
  P=PWM
  D=Direction
  C=Current
  Motor1 +
  Motor1 -
  Motor 2 +
  Motor2 -
  Motor3-
  Motor3+
  Motor4-
  Motor4+
  **Drive Motor**
  Right side/arm side
  **Drive Motor**
  Left side
  Elbow
  Shoulder
  Magnet
  Shoulder - 8
  Elbow - 9
  Enc2 - 3
  Enc1 - 2
  Enc4 - 20
  Enc3 - 21
  Motor1DIR - 22
  Motor2DIR - 23
  1 P/D/C
  2-P/D/C
  **Linear actuator**
  Wire so normal polarity goes down
